// Logisim project TallerLogica-Combinatorios.circ as structural Verilog: 12 circuits, main circuit sumador_simple
module sumador_simple (
  input  a,
  input  b,
  output S,
  output Cout
);

  xor xor_1 (S, a, b);
  and and_1 (Cout, a, b);
endmodule

module sumador_completo (
  input  Cin,
  input  A,
  input  B,
  output S,
  output Cout
);

  wire SS1_cout, SS1_s, SS2_cout;

  sumador_simple SS1 (.a(A), .b(B), .S(SS1_s), .Cout(SS1_cout));
  sumador_simple SS2 (.a(Cin), .b(SS1_s), .S(S), .Cout(SS2_cout));
  xor xor_1 (Cout, SS2_cout, SS1_cout);

  // Notes on the sheet:
  //   sum
  //   Co
  //   sum
  //   Co
endmodule

module sumador_4 (
  input  Cin,
  input  [3:0] A,
  input  [3:0] B,
  output [3:0] S,
  output Cout
);

  wire sumador_completo_1_cout, sumador_completo_2_cout, sumador_completo_3_cout;

  sumador_completo sumador_completo_1 (.A(A[0]), .B(B[0]), .Cin(Cin), .S(S[0]), .Cout(sumador_completo_1_cout));
  sumador_completo sumador_completo_2 (
    .A(A[1]), .B(B[1]), .Cin(sumador_completo_1_cout), .S(S[1]), .Cout(sumador_completo_2_cout));
  sumador_completo sumador_completo_3 (
    .A(A[2]), .B(B[2]), .Cin(sumador_completo_2_cout), .S(S[2]), .Cout(sumador_completo_3_cout));
  sumador_completo sumador_completo_4 (.A(A[3]), .B(B[3]), .Cin(sumador_completo_3_cout), .S(S[3]), .Cout(Cout));
  Hex_Digit_Display hex_digit_display_1 (.value(S));  // open: dp
endmodule

module comparador_cero (
  input  [3:0] A,
  output Z
);

  wire and_1_out, and_2_out, not_1_out, not_2_out, not_3_out, not_4_out;

  not not_1 (not_1_out, A[0]);
  and and_1 (and_1_out, not_1_out, not_2_out);
  not not_2 (not_2_out, A[1]);
  not not_3 (not_3_out, A[2]);
  and and_2 (and_2_out, not_3_out, not_4_out);
  not not_4 (not_4_out, A[3]);
  and and_3 (Z, and_1_out, and_2_out);
endmodule

module sumador_flags (
  input  Cin,
  input  [3:0] A,
  input  [3:0] B,
  output [3:0] S,
  output N,
  output Z,
  output V,
  output C
);

  sumador_4 sumador_4_1 (.Cin(Cin), .A(A), .S({N, S[2:0]}), .B(B), .Cout(C));
  comparador_overflow Comp_V (.A(A), .B(B), .S({N, S[2:0]}), .V(V));
  Hex_Digit_Display hex_digit_display_1 (.value({N, S[2:0]}));  // open: dp
  comparador_cero Comp_Z (.A({N, S[2:0]}), .Z(Z));

  assign S[3] = N;
endmodule

module incrementador_4 (
  input  [3:0] A,
  output [3:0] S
);

  sumador_4 sumador_4_1 (.Cin(1'b0), .A(A), .S(S), .B(4'b0001));  // open: Cout
  Hex_Digit_Display hex_digit_display_1 (.value(S));  // open: dp
endmodule

module inversor_4 (
  input  [3:0] A,
  input  INV,
  output [3:0] S
);

  wire [3:0] INC_s, not_1_out;

  not not_1 (not_1_out[0], A[0]);
  not not_2 (not_1_out[1], A[1]);
  not not_3 (not_1_out[2], A[2]);
  not not_4 (not_1_out[3], A[3]);
  incrementador_4 INC (.A(not_1_out), .S(INC_s));
  Multiplexer #(.width(4), .enable("false")) multiplexer_1 (.in0(A), .in1(INC_s), .out(S), .sel(INV));
  Hex_Digit_Display hex_digit_display_1 (.value(S));  // open: dp
endmodule

module ALU (
  input  [3:0] A,
  input  [3:0] B,
  input  [1:0] OP,
  output N,
  output Z,
  output V,
  output C,
  output [3:0] S
);

  wire [1:0] AND_F_n, OR_F_n;
  wire [3:0] AND_F_s, OR_F_s, Rest_F_n, Rest_F_s, Sum_F_n, Sum_F_s;

  sumador_flags Sum_F (
    .A(A), .B(B), .Cin(1'b0), .S(Sum_F_s), .N(Sum_F_n[0]), .Z(Sum_F_n[1]), .V(Sum_F_n[2]), .C(Sum_F_n[3]));
  restador_flags Rest_F (
    .A(A), .B(B), .S(Rest_F_s), .N(Rest_F_n[0]), .Z(Rest_F_n[1]), .V(Rest_F_n[2]), .C(Rest_F_n[3]));
  and_flags AND_F (.A(A), .B(B), .S(AND_F_s), .N(AND_F_n[0]), .Z(AND_F_n[1]));
  or_flags OR_F (.A(A), .B(B), .S(OR_F_s), .N(OR_F_n[0]), .Z(OR_F_n[1]));
  Multiplexer #(.select(2), .width(4), .enable("false")) multiplexer_1 (
    .in0(Sum_F_s), .in1(Rest_F_s), .in2(AND_F_s), .in3(OR_F_s), .out(S), .sel(OP));
  Multiplexer #(.select(2), .width(4), .enable("false")) multiplexer_2 (
    .in0(Sum_F_n), .in1(Rest_F_n), .in2({2'b00, AND_F_n}), .in3({2'b00, OR_F_n}), .out({C, V, Z, N}), .sel(OP));
  Hex_Digit_Display hex_digit_display_1 (.value(S));  // open: dp
endmodule

module comparador_overflow (
  input  [3:0] A,
  input  [3:0] B,
  input  [3:0] S,
  output V
);

  wire not_1_out, xor_1_out, xor_2_out;

  xor xor_1 (xor_1_out, A[3], B[3]);
  not not_1 (not_1_out, xor_1_out);
  xor xor_2 (xor_2_out, B[3], S[3]);
  and and_1 (V, not_1_out, xor_2_out);
endmodule

module restador_flags (
  input  [3:0] A,
  input  [3:0] B,
  output [3:0] S,
  output N,
  output Z,
  output V,
  output C
);

  wire sumador_flags_1_c;
  wire [3:0] INV_s;

  inversor_4 INV (.A(B), .INV(1'b1), .S(INV_s));
  sumador_flags sumador_flags_1 (.A(A), .B(INV_s), .Cin(1'b0), .S(S), .N(N), .Z(Z), .V(V), .C(sumador_flags_1_c));
  not not_1 (C, sumador_flags_1_c);
endmodule

module and_flags (
  input  [3:0] A,
  input  [3:0] B,
  output [3:0] S,
  output N,
  output Z
);

  and and_1 (S[0], A[0], B[0]);
  and and_2 (S[1], A[1], B[1]);
  and and_3 (S[2], A[2], B[2]);
  and and_4 (N, A[3], B[3]);
  comparador_cero Comp_Z (.A({N, S[2:0]}), .Z(Z));

  assign S[3] = N;
endmodule

module or_flags (
  input  [3:0] A,
  input  [3:0] B,
  output [3:0] S,
  output N,
  output Z
);

  or or_1 (S[0], A[0], B[0]);
  or or_2 (S[1], A[1], B[1]);
  or or_3 (S[2], A[2], B[2]);
  or or_4 (N, A[3], B[3]);
  comparador_cero Comp_Z (.A({N, S[2:0]}), .Z(Z));

  assign S[3] = N;
endmodule
